// Logisim project Obligatorio1 Infra(pre final).circ as structural Verilog: 17 circuits, main circuit Main
module Main (
  input  [2:0] Operacion,
  input  [2:0] Input_1,
  input  [2:0] Input_2,
  input  CS
);

  wire aux_zerohandler_1_out_5, decoder_1_out0, decoder_1_out1, decoder_1_out2, decoder_1_out3,
       decoder_1_out4, decoder_1_out5, decoder_1_out6, decoder_1_out7, op000_write_1_cs_000,
       op000_write_1_write, op001_read_1_cs_001, op001_read_1_read, op010_sum_1_c_out, op100_reset_1_cs_100,
       op100_reset_1_reset, op111_resta_1_overflow, or_1_out, or_2_out, sis_memoria_1_empty,
       sis_memoria_1_full;
  wire [2:0] op000_write_1_out_w, op000_write_1_pos_w, op010_sum_1_out_1, sis_ingresopalabras_1_out_abc,
       sis_ingresopalabras_1_out_def, sis_ingresopalabras_1_out_ghi;

  Sis_IngresoPalabras sis_ingresopalabras_1 (
    .IN_ABC(Operacion), .IN_DEF(Input_1), .IN_GHI(Input_2), .CS(CS), .OUT_ABC(sis_ingresopalabras_1_out_abc),
    .OUT_DEF(sis_ingresopalabras_1_out_def), .OUT_GHI(sis_ingresopalabras_1_out_ghi));
  Decoder #(.select(3)) decoder_1 (
    .out0(decoder_1_out0), .out1(decoder_1_out1), .out2(decoder_1_out2), .out3(decoder_1_out3),
    .out4(decoder_1_out4), .out5(decoder_1_out5), .out6(decoder_1_out6), .out7(decoder_1_out7),
    .sel(sis_ingresopalabras_1_out_abc), .en(CS));
  Op000_Write op000_write_1 (
    .CS(decoder_1_out0), .GHI(sis_ingresopalabras_1_out_ghi), .DEF(sis_ingresopalabras_1_out_def),
    .WRITE(op000_write_1_write), .CS_000(op000_write_1_cs_000), .OUT_W(op000_write_1_out_w),
    .POS_W(op000_write_1_pos_w));
  Op001_Read op001_read_1 (
    .CS(decoder_1_out1), .DEF(sis_ingresopalabras_1_out_def), .READ(op001_read_1_read),
    .CS_001(op001_read_1_cs_001), .POS(op000_write_1_pos_w));
  Op010_Sum op010_sum_1 (
    .C_IN(1'b0), .IN_1(sis_ingresopalabras_1_out_ghi), .IN_2(sis_ingresopalabras_1_out_def),
    .CS(decoder_1_out2), .C_OUT(op010_sum_1_c_out), .OUT_1(op010_sum_1_out_1));
  Op011_F1 op011_f1_1 (
    .DEF(sis_ingresopalabras_1_out_def), .GHI(sis_ingresopalabras_1_out_ghi), .CS(decoder_1_out3),
    .O(op010_sum_1_out_1));
  Op100_Reset op100_reset_1 (.CS(decoder_1_out4), .CS_100(op100_reset_1_cs_100), .RESET(op100_reset_1_reset));
  Op101_F2 op101_f2_1 (
    .DEF(sis_ingresopalabras_1_out_def), .GHI(sis_ingresopalabras_1_out_ghi), .CS(decoder_1_out5),
    .out_4(op010_sum_1_out_1));
  Op110_CA2 op110_ca2_1 (
    .in_1(sis_ingresopalabras_1_out_def), .CS(decoder_1_out6), .OUT_1(op010_sum_1_out_1));  // open: C_Out
  Op111_Resta op111_resta_1 (
    .DEF(sis_ingresopalabras_1_out_def), .GHI(sis_ingresopalabras_1_out_ghi), .CS(decoder_1_out7),
    .OUT_O(op010_sum_1_out_1), .Overflow(op111_resta_1_overflow));
  or or_1 (or_1_out, op000_write_1_cs_000, op100_reset_1_cs_100, op001_read_1_cs_001);
  Sis_Memoria sis_memoria_1 (
    .Datos(op000_write_1_out_w), .Write(op000_write_1_write), .Read(op001_read_1_read),
    .Reset(op100_reset_1_reset), .CS(or_1_out), .Posicion(op000_write_1_pos_w), .OUT_0(op010_sum_1_out_1),
    .Empty(sis_memoria_1_empty), .Full(sis_memoria_1_full));
  LED Empty_Word_Flag (.in(sis_memoria_1_empty));
  LED Full_Memory_Flag (.in(sis_memoria_1_full));
  LED Carry_Flag (.in(op010_sum_1_c_out));
  or or_2 (or_2_out, op010_sum_1_c_out, op111_resta_1_overflow);
  LED Overflow_Flag (.in(or_2_out));
  LED Zero_Flag (.in(aux_zerohandler_1_out_5));
  Aux_ZeroHandler aux_zerohandler_1 (
    .DATA_010(op010_sum_1_out_1), .CS_010(decoder_1_out2), .DATA_111(op010_sum_1_out_1),
    .CS_111(decoder_1_out7), .out_5(aux_zerohandler_1_out_5));
  LED led_1 (.in(op010_sum_1_out_1[2]));
  LED led_2 (.in(op010_sum_1_out_1[1]));
  LED led_3 (.in(op010_sum_1_out_1[0]));
endmodule

// memoria
module Sis_Memoria (
  input  [2:0] Datos,
  input  Write,
  input  Read,
  input  Reset,
  input  CS,
  input  [2:0] Posicion,
  output [2:0] OUT_0,
  output Empty,
  output Full
);

  wire decoder_1_out0, decoder_1_out1, decoder_1_out2, decoder_1_out3, decoder_1_out4, decoder_1_out5,
       decoder_1_out6, decoder_1_out7;
  wire [2:0] aux_tresbitflipflop_1_state, aux_tresbitflipflop_2_state, aux_tresbitflipflop_3_state,
       aux_tresbitflipflop_4_state, aux_tresbitflipflop_5_state, aux_tresbitflipflop_6_state,
       aux_tresbitflipflop_7_state, aux_tresbitflipflop_8_state;

  Decoder #(.select(3)) decoder_1 (
    .out0(decoder_1_out0), .out1(decoder_1_out1), .out2(decoder_1_out2), .out3(decoder_1_out3),
    .out4(decoder_1_out4), .out5(decoder_1_out5), .out6(decoder_1_out6), .out7(decoder_1_out7),
    .sel(Posicion), .en(CS));
  Aux_TresBitFlipFlop aux_tresbitflipflop_1 (
    .Datos(Datos), .Write(Write), .Read(Read), .CS(decoder_1_out0), .Reset(Reset), .Out_1(OUT_0),
    .State(aux_tresbitflipflop_1_state));
  Aux_TresBitFlipFlop aux_tresbitflipflop_2 (
    .Datos(Datos), .Write(Write), .Read(Read), .CS(decoder_1_out1), .Reset(Reset), .Out_1(OUT_0),
    .State(aux_tresbitflipflop_2_state));
  Aux_TresBitFlipFlop aux_tresbitflipflop_3 (
    .Datos(Datos), .Write(Write), .Read(Read), .CS(decoder_1_out2), .Reset(Reset), .Out_1(OUT_0),
    .State(aux_tresbitflipflop_3_state));
  Aux_TresBitFlipFlop aux_tresbitflipflop_4 (
    .Datos(Datos), .Write(Write), .Read(Read), .CS(decoder_1_out3), .Reset(Reset), .Out_1(OUT_0),
    .State(aux_tresbitflipflop_4_state));
  Aux_TresBitFlipFlop aux_tresbitflipflop_5 (
    .Datos(Datos), .Write(Write), .Read(Read), .CS(decoder_1_out4), .Reset(Reset), .Out_1(OUT_0),
    .State(aux_tresbitflipflop_5_state));
  Aux_TresBitFlipFlop aux_tresbitflipflop_6 (
    .Datos(Datos), .Write(Write), .Read(Read), .CS(decoder_1_out5), .Reset(Reset), .Out_1(OUT_0),
    .State(aux_tresbitflipflop_6_state));
  Aux_TresBitFlipFlop aux_tresbitflipflop_7 (
    .Datos(Datos), .Write(Write), .Read(Read), .CS(decoder_1_out6), .Reset(Reset), .Out_1(OUT_0),
    .State(aux_tresbitflipflop_7_state));
  Aux_TresBitFlipFlop aux_tresbitflipflop_8 (
    .Datos(Datos), .Write(Write), .Read(Read), .CS(decoder_1_out7), .Reset(Reset), .Out_1(OUT_0),
    .State(aux_tresbitflipflop_8_state));
  Aux_EmptyWord aux_emptyword_1 (
    .in_1(aux_tresbitflipflop_1_state), .in_2(aux_tresbitflipflop_2_state),
    .in_3(aux_tresbitflipflop_3_state), .in_4(aux_tresbitflipflop_4_state),
    .in_5(aux_tresbitflipflop_5_state), .in_6(aux_tresbitflipflop_6_state),
    .in_7(aux_tresbitflipflop_7_state), .in_8(aux_tresbitflipflop_8_state), .out_9(Empty));
  Aux_FullMemory aux_fullmemory_1 (
    .in_1(aux_tresbitflipflop_1_state), .in_2(aux_tresbitflipflop_2_state),
    .in_3(aux_tresbitflipflop_3_state), .in_4(aux_tresbitflipflop_4_state),
    .in_5(aux_tresbitflipflop_5_state), .in_6(aux_tresbitflipflop_6_state),
    .in_7(aux_tresbitflipflop_7_state), .in_8(aux_tresbitflipflop_8_state), .out_9(Full));
endmodule

module Aux_TresBitFlipFlop (
  input  [2:0] Datos,
  input  Write,
  input  Read,
  input  CS,
  input  Reset,
  output [2:0] Out_1,
  output [2:0] State
);

  wire and_1_out, and_2_out;

  and and_1 (and_1_out, Write, CS);
  and and_2 (and_2_out, Read, CS);
  D_Flip_Flop d_ff_1 (.D(Datos[0]), .clk(and_1_out), .Q(State[0]), .reset(Reset));  // open: Qn, preset
  D_Flip_Flop d_ff_2 (.D(Datos[1]), .clk(and_1_out), .Q(State[1]), .reset(Reset));  // open: Qn, preset
  D_Flip_Flop d_ff_3 (.D(Datos[2]), .clk(and_1_out), .Q(State[2]), .reset(Reset));  // open: Qn, preset
  assign Out_1 = and_2_out ? State : 3'bz;  // Controlled_Buffer controlled_buffer_1
endmodule

module Sis_IngresoPalabras (
  input  [2:0] IN_ABC,
  input  [2:0] IN_DEF,
  input  [2:0] IN_GHI,
  input  CS,
  output [2:0] OUT_ABC,
  output [2:0] OUT_DEF,
  output [2:0] OUT_GHI
);

  assign OUT_ABC = CS ? IN_ABC : 3'bz;  // Controlled_Buffer controlled_buffer_1
  assign OUT_DEF = CS ? IN_DEF : 3'bz;  // Controlled_Buffer controlled_buffer_2
  assign OUT_GHI = CS ? IN_GHI : 3'bz;  // Controlled_Buffer controlled_buffer_3
endmodule

module Op010_Sum (
  input  C_IN,
  input  [2:0] IN_1,
  input  [2:0] IN_2,
  input  CS,
  output C_OUT,
  output [2:0] OUT_1
);

  wire adder_1_cout;
  wire [2:0] adder_1_out;

  Adder #(.width(3)) adder_1 (.a(IN_1), .b(IN_2), .out(adder_1_out), .cin(C_IN), .cout(adder_1_cout));
  and and_1 (C_OUT, adder_1_cout, CS);
  assign OUT_1 = CS ? adder_1_out : 3'bz;  // Controlled_Buffer controlled_buffer_1
endmodule

module Op000_Write (
  input  CS,
  input  [2:0] GHI,
  input  [2:0] DEF,
  output WRITE,
  output CS_000,
  output [2:0] OUT_W,
  output [2:0] POS_W
);


  assign CS_000 = CS;
  assign OUT_W = GHI;
  assign POS_W = DEF;
  assign WRITE = CS;
endmodule

module Op001_Read (
  input  CS,
  input  [2:0] DEF,
  output READ,
  output CS_001,
  output [2:0] POS
);


  assign CS_001 = CS;
  assign POS = DEF;
  assign READ = CS;
endmodule

module Op100_Reset (
  input  CS,
  output CS_100,
  output RESET
);


  assign CS_100 = CS;
  assign RESET = CS;
endmodule

module Op011_F1 (
  input  [2:0] DEF,
  input  [2:0] GHI,
  input  CS,
  output [2:0] O
);

  wire and_1_out, and_2_out, and_3_out, and_4_out, not_1_out, not_2_out, not_3_out, not_4_out, or_1_out;
  wire [0:0] controlled_buffer_1_out;

  not not_1 (not_1_out, DEF[0]);
  not not_2 (not_2_out, DEF[1]);
  not not_3 (not_3_out, DEF[2]);
  not not_4 (not_4_out, GHI[0]);
  and and_1 (and_1_out, not_1_out, not_2_out, not_3_out, not_4_out);
  and and_2 (and_2_out, DEF[1], DEF[2], not_4_out);
  and and_3 (and_3_out, DEF[0], not_2_out, not_3_out, GHI[0]);
  and and_4 (and_4_out, DEF[0], DEF[1], DEF[2]);
  or or_1 (or_1_out, and_1_out, and_2_out, and_3_out, and_4_out);
  assign controlled_buffer_1_out[0] = CS ? or_1_out : 1'bz;  // Controlled_Buffer controlled_buffer_1
  assign O = CS ? {2'b00, controlled_buffer_1_out[0]} : 3'bz;  // Controlled_Buffer controlled_buffer_2
endmodule

module Op101_F2 (
  input  [2:0] DEF,
  input  [2:0] GHI,
  input  CS,
  output [2:0] out_4
);

  wire controlled_buffer_1_out, controlled_buffer_2_out, controlled_buffer_3_out, controlled_buffer_4_out,
       controlled_buffer_5_out, controlled_buffer_6_out, xor_1_out, xor_2_out, xor_3_out, xor_4_out;
  wire [0:0] xor_5_out;

  assign controlled_buffer_1_out = CS ? DEF[0] : 1'bz;  // Controlled_Buffer controlled_buffer_1
  assign controlled_buffer_2_out = CS ? DEF[1] : 1'bz;  // Controlled_Buffer controlled_buffer_2
  assign controlled_buffer_3_out = CS ? DEF[2] : 1'bz;  // Controlled_Buffer controlled_buffer_3
  assign controlled_buffer_4_out = CS ? GHI[0] : 1'bz;  // Controlled_Buffer controlled_buffer_4
  assign controlled_buffer_5_out = CS ? GHI[1] : 1'bz;  // Controlled_Buffer controlled_buffer_5
  assign controlled_buffer_6_out = CS ? GHI[2] : 1'bz;  // Controlled_Buffer controlled_buffer_6
  xor xor_1 (xor_1_out, controlled_buffer_1_out, controlled_buffer_2_out);
  xor xor_2 (xor_2_out, controlled_buffer_3_out, controlled_buffer_4_out);
  xor xor_3 (xor_3_out, controlled_buffer_5_out, controlled_buffer_6_out);
  xor xor_4 (xor_4_out, xor_1_out, xor_2_out);
  xor xor_5 (xor_5_out[0], xor_4_out, xor_3_out);
  assign out_4 = CS ? {2'b00, xor_5_out[0]} : 3'bz;  // Controlled_Buffer controlled_buffer_7
endmodule

module Op110_CA2 (
  input  [2:0] in_1,
  input  CS,
  output [2:0] OUT_1,
  output C_Out
);

  wire not_1_out, not_2_out, not_3_out;
  wire [2:0] adder_1_out, controlled_buffer_1_out;

  not not_1 (not_1_out, in_1[0]);
  not not_2 (not_2_out, in_1[1]);
  assign controlled_buffer_1_out[0] = CS ? not_1_out : 1'bz;  // Controlled_Buffer controlled_buffer_1
  assign controlled_buffer_1_out[1] = CS ? not_2_out : 1'bz;  // Controlled_Buffer controlled_buffer_2
  not not_3 (not_3_out, in_1[2]);
  assign controlled_buffer_1_out[2] = CS ? not_3_out : 1'bz;  // Controlled_Buffer controlled_buffer_3
  assign OUT_1 = CS ? adder_1_out : 3'bz;  // Controlled_Buffer controlled_buffer_4
  Adder #(.width(3)) adder_1 (.a(controlled_buffer_1_out), .b(3'b001), .out(adder_1_out), .cout(C_Out));  // open: cin
endmodule

module Op111_Resta (
  input  [2:0] DEF,
  input  [2:0] GHI,
  input  CS,
  output [2:0] OUT_O,
  output Overflow
);

  wire and_1_out, subtractor_1_bout;
  wire [1:0] subtractor_1_out;

  Subtractor #(.width(2)) subtractor_1 (
    .a(DEF[2:1]), .b({DEF[0], GHI[2]}), .out(subtractor_1_out), .bin(1'b0), .bout(subtractor_1_bout));
  assign OUT_O = and_1_out ? {1'b0, subtractor_1_out} : 3'bz;  // Controlled_Buffer controlled_buffer_1
  and and_1 (and_1_out, ~subtractor_1_bout, CS);  // AND_Gate
  and and_2 (Overflow, subtractor_1_bout, CS);
endmodule

module Aux_EsCero (
  input  [2:0] IN_1,
  input  CS,
  output OUT_1
);

  wire and_1_out, controlled_buffer_1_out, controlled_buffer_2_out, controlled_buffer_3_out, not_1_out,
       not_2_out, not_3_out;

  assign controlled_buffer_1_out = CS ? IN_1[0] : 1'bz;  // Controlled_Buffer controlled_buffer_1
  assign controlled_buffer_2_out = CS ? IN_1[1] : 1'bz;  // Controlled_Buffer controlled_buffer_2
  assign controlled_buffer_3_out = CS ? IN_1[2] : 1'bz;  // Controlled_Buffer controlled_buffer_3
  not not_1 (not_1_out, controlled_buffer_1_out);
  not not_2 (not_2_out, controlled_buffer_2_out);
  not not_3 (not_3_out, controlled_buffer_3_out);
  and and_1 (and_1_out, not_1_out, not_2_out, not_3_out);
  assign OUT_1 = CS ? and_1_out : 1'bz;  // Controlled_Buffer controlled_buffer_4
endmodule

module Aux_EmptyWord (
  input  [2:0] in_1,
  input  [2:0] in_2,
  input  [2:0] in_3,
  input  [2:0] in_4,
  input  [2:0] in_5,
  input  [2:0] in_6,
  input  [2:0] in_7,
  input  [2:0] in_8,
  output out_9
);

  wire aux_escero_1_out_1, aux_escero_2_out_1, aux_escero_3_out_1, aux_escero_4_out_1, aux_escero_5_out_1,
       aux_escero_6_out_1, aux_escero_7_out_1, aux_escero_8_out_1;

  Aux_EsCero aux_escero_1 (.IN_1(in_1), .CS(1'b1), .OUT_1(aux_escero_1_out_1));
  Aux_EsCero aux_escero_2 (.IN_1(in_2), .CS(1'b1), .OUT_1(aux_escero_2_out_1));
  Aux_EsCero aux_escero_3 (.IN_1(in_3), .CS(1'b1), .OUT_1(aux_escero_3_out_1));
  Aux_EsCero aux_escero_4 (.IN_1(in_4), .CS(1'b1), .OUT_1(aux_escero_4_out_1));
  Aux_EsCero aux_escero_5 (.IN_1(in_5), .CS(1'b1), .OUT_1(aux_escero_5_out_1));
  Aux_EsCero aux_escero_6 (.IN_1(in_6), .CS(1'b1), .OUT_1(aux_escero_6_out_1));
  Aux_EsCero aux_escero_7 (.IN_1(in_7), .CS(1'b1), .OUT_1(aux_escero_7_out_1));
  Aux_EsCero aux_escero_8 (.IN_1(in_8), .CS(1'b1), .OUT_1(aux_escero_8_out_1));
  or or_1 (out_9, aux_escero_1_out_1, aux_escero_2_out_1, aux_escero_3_out_1, aux_escero_4_out_1, aux_escero_5_out_1, aux_escero_6_out_1, aux_escero_7_out_1, aux_escero_8_out_1);
endmodule

module Aux_FullMemory (
  input  [2:0] in_1,
  input  [2:0] in_2,
  input  [2:0] in_3,
  input  [2:0] in_4,
  input  [2:0] in_5,
  input  [2:0] in_6,
  input  [2:0] in_7,
  input  [2:0] in_8,
  output out_9
);

  wire aux_essiete_1_out_1, aux_essiete_2_out_1, aux_essiete_3_out_1, aux_essiete_4_out_1,
       aux_essiete_5_out_1, aux_essiete_6_out_1, aux_essiete_7_out_1, aux_essiete_8_out_1;

  Aux_EsSiete aux_essiete_1 (.IN_1(in_1), .CS(1'b1), .OUT_1(aux_essiete_1_out_1));
  Aux_EsSiete aux_essiete_2 (.IN_1(in_2), .CS(1'b1), .OUT_1(aux_essiete_2_out_1));
  Aux_EsSiete aux_essiete_3 (.IN_1(in_3), .CS(1'b1), .OUT_1(aux_essiete_3_out_1));
  Aux_EsSiete aux_essiete_4 (.IN_1(in_4), .CS(1'b1), .OUT_1(aux_essiete_4_out_1));
  Aux_EsSiete aux_essiete_5 (.IN_1(in_5), .CS(1'b1), .OUT_1(aux_essiete_5_out_1));
  Aux_EsSiete aux_essiete_6 (.IN_1(in_6), .CS(1'b1), .OUT_1(aux_essiete_6_out_1));
  Aux_EsSiete aux_essiete_7 (.IN_1(in_7), .CS(1'b1), .OUT_1(aux_essiete_7_out_1));
  Aux_EsSiete aux_essiete_8 (.IN_1(in_8), .CS(1'b1), .OUT_1(aux_essiete_8_out_1));
  and and_1 (out_9, aux_essiete_1_out_1, aux_essiete_2_out_1, aux_essiete_3_out_1, aux_essiete_4_out_1, aux_essiete_5_out_1, aux_essiete_6_out_1, aux_essiete_7_out_1, aux_essiete_8_out_1);
endmodule

module Aux_EsSiete (
  input  [2:0] IN_1,
  input  CS,
  output OUT_1
);

  wire and_1_out, controlled_buffer_1_out, controlled_buffer_2_out, controlled_buffer_3_out;

  assign controlled_buffer_1_out = CS ? IN_1[0] : 1'bz;  // Controlled_Buffer controlled_buffer_1
  assign controlled_buffer_2_out = CS ? IN_1[1] : 1'bz;  // Controlled_Buffer controlled_buffer_2
  assign controlled_buffer_3_out = CS ? IN_1[2] : 1'bz;  // Controlled_Buffer controlled_buffer_3
  and and_1 (and_1_out, controlled_buffer_1_out, controlled_buffer_2_out, controlled_buffer_3_out);
  assign OUT_1 = CS ? and_1_out : 1'bz;  // Controlled_Buffer controlled_buffer_4
endmodule

module Aux_ZeroHandler (
  input  [2:0] DATA_010,
  input  CS_010,
  input  [2:0] DATA_111,
  input  CS_111,
  output out_5
);

  wire or_1_out;
  wire [2:0] controlled_buffer_1_out;

  assign controlled_buffer_1_out = CS_010 ? DATA_010 : 3'bz;  // Controlled_Buffer controlled_buffer_1
  assign controlled_buffer_1_out = CS_111 ? DATA_111 : 3'bz;  // Controlled_Buffer controlled_buffer_2
  or or_1 (or_1_out, CS_010, CS_111);
  Aux_EsCero aux_escero_1 (.IN_1(controlled_buffer_1_out), .CS(or_1_out), .OUT_1(out_5));
endmodule
